// Logisim project trabalho_3.circ as structural Verilog: 6 circuits, main circuit PC_e_MI
module trabalho (
  output [7:0] out_1
);

  wire ALUSrc, Branch, clk, Incr, MemtoReg, MemWr_3, not_1_out, PcSrc, PCSumSrc, RegWr, Reset_out, Zero;
  wire [3:0] ALUOp, banco_de_registradores_2_p7;
  wire [7:0] adder_1_out, banco_de_registradores_2_p1, data, Imm, multiplexer_1_out, multiplexer_2_out,
       multiplexer_3_out, ra, ra_2, rb, rb_2, TA, ula_1_out_7;
  wire [31:0] pc_e_mi_1_instr;

  Adder adder_1 (.a(out_1), .b(8'h1), .out(adder_1_out), .cin(1'b0));  // open: cout
  Multiplexer #(.width(8)) multiplexer_1 (.in0(adder_1_out), .in1(TA), .out(multiplexer_1_out), .sel(PcSrc));
  not not_1 (not_1_out, clk);
  Clock clock_1 (.out(clk));
  PC_e_MI pc_e_mi_1 (
    .clk(not_1_out), .PC(multiplexer_1_out), .d(ra_2), .MemWr(MemWr_3), .addr(rb_2), .out_7(out_1),
    .instr(pc_e_mi_1_instr), .data(data));
  banco_de_registradores banco_de_registradores_1 ();  // open: in_13, rb, in_7, in_11, in_12, in_14, in_10, ra, in_4, in_5, Dado, Reset, ALUSrc, clk, saida_2, out_21, out_22, saida_1, out_17, out_18, out_19, out_20
  Button Reset (.out(Reset_out));
  // NOT_Gate not_2 has open pins: in=clk, out=open
  unidade_de_controle unidade_de_controle_1 (
    .opcode(banco_de_registradores_2_p1[7:4]), .ALUSrc(ALUSrc), .Branch(Branch), .RegWr(RegWr),
    .MemtoReg(MemtoReg), .PcSumSrc(PCSumSrc), .Incr(Incr), .ALUOp(ALUOp));
  Multiplexer #(.width(8)) multiplexer_2 (.in0(ula_1_out_7), .in1(data), .out(multiplexer_2_out), .sel(MemtoReg));
  assign Imm = {{4{banco_de_registradores_2_p7[3]}}, banco_de_registradores_2_p7};  // Bit_Extender bit_extender_1
  // banco_de_registradores banco_de_registradores_2: pin names not known; wires that end beside it: banco_de_registradores_2_p1[3:0], Reset_out, RegWr, banco_de_registradores_2_p1[1:0], banco_de_registradores_2_p1[3:2], ALUSrc, banco_de_registradores_2_p7, multiplexer_2_out, rb, ra
  Multiplexer #(.width(8)) multiplexer_3 (.in0(rb), .in1(Imm), .out(multiplexer_3_out), .sel(ALUSrc));
  ULA ula_1 (
    .Branch(Branch), .Incr(Incr), .rb(multiplexer_3_out), .ra(ra), .ALUOp(ALUOp), .out_7(ula_1_out_7),
    .zero(Zero));

  // Other names for the same wires on the sheet: PC[7:0] = out_1
endmodule

module PC_e_MI (
  input  [7:0] addr,
  input  [7:0] PC,
  input  clk,
  input  MemWr,
  input  [7:0] d,
  output [31:0] instr,
  output [7:0] out_7,
  output [7:0] data
);

  wire button_1_out;
  wire [31:0] bit_extender_1_out;
  wire [31:8] dual_port_ram_1_data;

  Register register_1 (.D(PC), .en(1'b1), .clk(clk), .Q(out_7), .clr(button_1_out));
  Button button_1 (.out(button_1_out));
  assign bit_extender_1_out = {{24{1'b0}}, d};  // Bit_Extender bit_extender_1
  dual_port_ram dual_port_ram_1 (
    .addr(addr), .pc(out_7), .d(bit_extender_1_out), .w(MemWr), .clk(clk), .instr(instr),
    .data({dual_port_ram_1_data, data}));
endmodule

module dual_port_ram (
  input  [7:0] addr,
  input  [7:0] pc,
  input  [31:0] d,
  input  w,
  input  clk,
  output [31:0] instr,
  output [31:0] data
);

  wire or_1_out;
  wire [7:0] multiplexer_1_out;

  Multiplexer #(.width(8)) multiplexer_1 (.in0(addr), .in1(pc), .out(multiplexer_1_out), .sel(clk));
  RAM #(.asyncread("true"), .dataWidth(32)) ram_1 (
    .addr(multiplexer_1_out), .we(or_1_out), .oe(1'b1), .clk(clk), .din(d), .dout(data));
  or or_1 (or_1_out, w, clk);
  Register #(.trigger("falling"), .width(32)) pcbuf (.D(data), .en(1'b1), .clk(clk), .Q(instr));  // open: clr
endmodule

module banco_de_registradores (
  input  [1:0] rb,
  input  Reset,
  input  [1:0] ra,
  input  [7:0] in_4,
  input  [7:0] in_5,
  input  [7:0] Dado,
  input  [1:0] in_7,
  input  ALUSrc,
  input  clk,
  input  [1:0] in_10,
  input  [1:0] in_11,
  input  [1:0] in_12,
  input  [1:0] in_13,
  input  [1:0] in_14,
  output [7:0] saida_2,
  output [7:0] saida_1,
  output [7:0] out_17,
  output [7:0] out_18,
  output [7:0] out_19,
  output [7:0] out_20,
  output [7:0] out_21,
  output [7:0] out_22
);

  wire comparator_1_eq, comparator_2_eq, comparator_3_eq, l1, l2, l3, or_3_out, regwr_1, regwr_3, regwr_4,
       undriven, undriven_2, undriven_3;
  wire [1:0] or_1_out, rd_1, rd_2, rd_3, rd_4;
  wire [7:0] D, multiplexer_1_out, r0, r1, r2, r3;

  and and_1 (l1, regwr_1, comparator_1_eq);
  Comparator #(.width(2)) comparator_1 (.a(rd_1), .b(2'b00), .eq(comparator_1_eq));  // open: gt, lt
  and and_2 (l2, regwr_3, comparator_2_eq);
  Comparator #(.width(2)) comparator_2 (.a(rd_3), .b(2'b00), .eq(comparator_2_eq));  // open: gt, lt
  and and_3 (l3, regwr_4, comparator_3_eq);
  Comparator #(.width(2)) comparator_3 (.a(rd_4), .b(2'b00), .eq(comparator_3_eq));  // open: gt, lt
  or or_1 (or_1_out[0], l1, l3);
  or or_2 (or_1_out[1], l2, l3);
  or or_3 (or_3_out, l1, l2, l3);
  Multiplexer #(.select(2), .width(8)) multiplexer_1 (
    .in1(Dado), .in2(in_5), .in3(in_4), .out(multiplexer_1_out), .sel(or_1_out));  // open: in0
  Register u_r0 (.D(multiplexer_1_out), .en(or_3_out), .clk(clk), .Q(r0), .clr(Reset));
  Register u_r1 (.D(D), .en(undriven), .clk(clk), .Q(r1), .clr(Reset));
  Register u_r2 (.D(D), .en(undriven_2), .clk(clk), .Q(r2), .clr(Reset));
  Register u_r3 (.D(D), .en(undriven_3), .clk(clk), .Q(r3), .clr(Reset));
  Multiplexer #(.select(2), .width(8)) multiplexer_2 (.in0(r0), .in1(r1), .in2(r2), .in3(r3), .out(saida_2), .sel(rb));
  Multiplexer #(.select(2), .width(8)) multiplexer_3 (
    .in0(r0), .in1(r1), .in2(r2), .in3(r3), .out(saida_1), .sel(rd_1));
  Multiplexer #(.width(2)) multiplexer_4 (.in0(ra), .in1(2'b00), .out(rd_1), .sel(ALUSrc));
  Multiplexer #(.select(2), .width(8)) multiplexer_5 (.in0(r0), .in1(r1), .in2(r2), .in3(r3), .out(out_17), .sel(in_7));
  Multiplexer #(.select(2), .width(8)) multiplexer_6 (.in0(r0), .in1(r1), .in2(r2), .in3(r3), .out(out_18), .sel(rd_2));
  Multiplexer #(.width(2)) multiplexer_7 (.in0(in_10), .in1(2'b00), .out(rd_2), .sel(ALUSrc));
  Multiplexer #(.select(2), .width(8)) multiplexer_8 (
    .in0(r0), .in1(r1), .in2(r2), .in3(r3), .out(out_19), .sel(in_11));
  Multiplexer #(.select(2), .width(8)) multiplexer_9 (.in0(r0), .in1(r1), .in2(r2), .in3(r3), .out(out_20), .sel(rd_3));
  Multiplexer #(.width(2)) multiplexer_10 (.in0(in_12), .in1(2'b00), .out(rd_3), .sel(ALUSrc));
  Multiplexer #(.select(2), .width(8)) multiplexer_11 (
    .in0(r0), .in1(r1), .in2(r2), .in3(r3), .out(out_21), .sel(in_13));
  Multiplexer #(.select(2), .width(8)) multiplexer_12 (
    .in0(r0), .in1(r1), .in2(r2), .in3(r3), .out(out_22), .sel(rd_4));
  Multiplexer #(.width(2)) multiplexer_13 (.in0(in_14), .in1(2'b00), .out(rd_4), .sel(ALUSrc));

  // Other names for the same wires on the sheet: D1[7:0] = Dado; D2[7:0] = in_5; D3[7:0] = in_4
endmodule

module ULA (
  input  [7:0] rb,
  input  [7:0] ra,
  input  Branch,
  input  Incr,
  input  [3:0] ALUOp,
  output zero,
  output [7:0] out_7
);

  wire Shift;
  wire [2:0] multiplexer_2_out;
  wire [4:0] multiplexer_2_out_2;
  wire [7:0] adder_1_out, and_1_out, multiplexer_1_out, multiplexer_3_out, multiplexer_4_out,
       multiplier_1_out, not_1_out, or_1_out, shifter_1_out, shifter_2_out, subtractor_1_out, xor_1_out;

  Multiplexer #(.width(8)) multiplexer_1 (.in0(rb), .in1({8{1'b0}}), .out(multiplexer_1_out), .sel(Branch));
  Multiplexer #(.width(8)) multiplexer_2 (
    .in0(multiplexer_1_out), .in1(8'h1), .out({multiplexer_2_out_2, multiplexer_2_out}), .sel(Incr));
  Comparator comparator_1 (.a({multiplexer_2_out_2, multiplexer_2_out}), .b(8'h7), .gt(Shift));  // open: eq, lt
  Shifter shifter_1 (.in(ra), .\dist (multiplexer_2_out), .out(shifter_1_out));
  Shifter #(.shift("lr")) shifter_2 (.in(ra), .\dist (multiplexer_2_out), .out(shifter_2_out));
  Adder adder_1 (.a(ra), .b({multiplexer_2_out_2, multiplexer_2_out}), .out(adder_1_out));  // open: cin, cout
  Subtractor subtractor_1 (
    .a(ra), .b({multiplexer_2_out_2, multiplexer_2_out}), .out(subtractor_1_out));  // open: bin, bout
  assign not_1_out = ~{multiplexer_2_out_2, multiplexer_2_out};  // NOT_Gate not_1, 8 bits wide
  assign and_1_out = ra & {multiplexer_2_out_2, multiplexer_2_out};  // AND_Gate and_1, 8 bits wide
  assign or_1_out = ra | {multiplexer_2_out_2, multiplexer_2_out};  // OR_Gate or_1, 8 bits wide
  assign xor_1_out = ra ^ {multiplexer_2_out_2, multiplexer_2_out};  // XOR_Gate xor_1, 8 bits wide
  Multiplexer #(.width(8)) multiplexer_3 (.in0(shifter_1_out), .in1({8{1'b0}}), .out(multiplexer_3_out), .sel(Shift));
  Multiplexer #(.width(8)) multiplexer_4 (.in0(shifter_2_out), .in1({8{1'b0}}), .out(multiplexer_4_out), .sel(Shift));
  Multiplier multiplier_1 (
    .a(ra), .b({multiplexer_2_out_2, multiplexer_2_out}), .out(multiplier_1_out));  // open: cin, cout
  Multiplexer #(.select(4), .width(8)) multiplexer_5 (
    .in0(adder_1_out), .in1(subtractor_1_out), .in2(not_1_out), .in3(and_1_out), .in4(or_1_out),
    .in5(xor_1_out), .in6(multiplexer_3_out), .in7(multiplexer_4_out), .in8(multiplier_1_out),
    .in9({multiplexer_2_out_2, multiplexer_2_out}), .out(out_7), .sel(ALUOp));  // open: in10, in11, in12, in13, in14, in15
  Comparator comparator_2 (.a({8{1'b0}}), .b(out_7), .eq(zero));  // open: gt, lt

  // Notes on the sheet:
  //   para (ra - 0)
  //   mv
endmodule

module unidade_de_controle (
  input  [3:0] opcode,
  output [3:0] ALUOp,
  output ALUSrc,
  output Branch,
  output RegWr,
  output MemtoReg,
  output PcSumSrc,
  output Incr
);

  wire and_1_out, and_2_out, and_4_out, and_5_out, and_6_out, and_7_out, and_8_out, and_11_out, not_1_out,
       not_2_out, not_3_out, not_4_out;

  not not_1 (not_1_out, opcode[3]);
  not not_2 (not_2_out, opcode[2]);
  not not_3 (not_3_out, opcode[1]);
  not not_4 (not_4_out, opcode[0]);
  and and_1 (and_1_out, not_1_out, opcode[2], not_3_out, opcode[0]);
  or or_1 (ALUOp[3], and_1_out, and_2_out);
  and and_2 (and_2_out, not_1_out, opcode[2], opcode[1], not_4_out);
  and and_3 (ALUOp[2], opcode[3], opcode[1]);
  and and_4 (and_4_out, opcode[3], not_2_out, not_3_out);
  or or_2 (ALUOp[1], and_4_out, and_5_out);
  and and_5 (and_5_out, opcode[3], opcode[2], opcode[1]);
  and and_6 (and_6_out, not_1_out, not_2_out, not_3_out, not_4_out);
  and and_7 (and_7_out, not_1_out, opcode[2], opcode[1], not_4_out);
  or or_3 (ALUOp[0], and_6_out, and_7_out, and_8_out);
  and and_8 (and_8_out, opcode[3], opcode[0]);
  and and_9 (ALUSrc, not_1_out, opcode[2], not_3_out);
  and and_10 (Branch, not_4_out, not_3_out, not_2_out, not_1_out);
  and and_11 (and_11_out, opcode[1], not_4_out);
  or or_4 (RegWr, and_11_out, opcode[2], opcode[3]);
  and and_12 (MemtoReg, not_1_out, not_2_out, opcode[1], not_4_out);
  and and_13 (PcSumSrc, not_1_out, not_2_out, not_3_out, opcode[0]);
  and and_14 (Incr, not_1_out, opcode[2], opcode[1], opcode[0]);
endmodule
